# Fritzing sketch ZXUSBKB (saved by Fritzing 0.9.2b)
stripboards: 2

parts:
  J1 = female pin header, 5 pins [form="♀ (female)"]
  R1 = Resistor [tolerance=±5% resistance=10 package=THT]
  R2 = Resistor [tolerance=±5% resistance=10 package=THT]
  R3 = Resistor [tolerance=±5% resistance=10 package=THT]
  R4 = Resistor [tolerance=±5% resistance=10 package=THT]  # not connected
  R5 = Resistor [tolerance=±5% resistance=10 package=THT]
  R6 = Resistor [tolerance=±5% resistance=10 package=THT]
  S1 = Pushbutton [package="[SMD]"]
  J3 = male pin header, 1 pin [form="♂ (male)"]
  J4 = Piezo Speaker
  J5 = male pin header, 1 pin [form="♂ (male)"]
  U1 = DIODE-ZENER [package=diode-zener]  # not connected
  U2 = DIODE-ZENER [package=diode-zener]
  U3 = DIODE-ZENER [package=diode-zener]
  U4 = DIODE-ZENER [package=diode-zener]
  U5 = DIODE-ZENER [package=diode-zener]
  U6 = DIODE-ZENER [package=diode-zener]
  U7 = DIODE-ZENER [package=diode-zener]
  U8 = DIODE-ZENER [package=diode-zener]
  J7 = double row male pin header, 8 pins [form="♂ (male)"]
  J6 = female pin header, 8 pins [form="♀ (female)"]
  J6_2 = female pin header, 8 pins [form="♀ (female)"]
  J2 = double row male pin header, 8 pins [form="♂ (male)"]
  J8 = male pin header, 1 pin [form="♂ (male)"]
  Pro_Micro2 = Pro Micro

nets:
  N1: J1.pin1, J2.pin2, Pro_Micro2.D18/A0
  N2: J1.pin2, J2.pin3, Pro_Micro2.D19/A1
  N3: J1.pin3, R3.Pin_1, J2.pin4, Pro_Micro2.D20/A2
  N4: J1.pin4, R2.Pin_1, J2.pin5, Pro_Micro2.D21/A3
  N5: J1.pin5, R1.Pin_1, J2.pin6, Pro_Micro2.D15/SCLK
  N6: R1.Pin_0, R5.Pin_0, R6.Pin_0, J2.pin1, Pro_Micro2.VCC
  N7: R6.Pin_1, S1.Pin_3, S1.Pin_4, J3.pin1, J2.pin7, Pro_Micro2.D14/MISO
  N8: S1.Pin_1, S1.Pin_2, J4.pin1, J5.pin1, J8.pin1, Pro_Micro2.GND
  N9: J4.pin2, J2.pin8, Pro_Micro2.D10
  N10: U2.C, J7.pin1, J6.pin1, J6_2.pin1, Pro_Micro2.D2
  N11: U3.C, J7.pin3, J6.pin3, J6_2.pin3, Pro_Micro2.D4
  N12: U4.C, J7.pin2, J6.pin2, J6_2.pin2, Pro_Micro2.D3
  N13: U5.C, J7.pin4, J6.pin4, J6_2.pin4, Pro_Micro2.D5
  N14: U6.C, J7.pin5, J6.pin5, J6_2.pin5, Pro_Micro2.D6
  N15: U7.C, J7.pin6, J6.pin6, J6_2.pin6, Pro_Micro2.D7
  N16: U8.C, J7.pin7, J6.pin7, J6_2.pin7, Pro_Micro2.D8
  N17: J7.pin8, J6.pin8, J6_2.pin8, Pro_Micro2.D9

custom parts:
  Pro Micro: The SparkFun Pro Micro is a complete USB-based microcontoller development system, in a very small footprint, capable of implementing many types of projects. All programming can be done via the USB port.
